# Fritzing sketch block_display-output (saved by Fritzing 0.9.4)

parts:
  IC15 = IC, DIP package, 20 pins [chip_label=74HC273]
  IC16 = IC, DIP package, 20 pins [chip_label=74HC273]
  GND = female pin header, 1 pin [form="♀ (female)"]
  5V = female pin header, 1 pin [form="♀ (female)"]
  C20 = Ceramic Capacitor [capacitance=100nF package="100 mil [THT, multilayer]"]
  C19 = Ceramic Capacitor [capacitance=100nF package="100 mil [THT, multilayer]"]
  IC13 = IC, DIP package, 16 pins [chip_label=74AC138]
  IC14 = IC, DIP package, 16 pins [chip_label=74AC138]
  C17 = Ceramic Capacitor [capacitance=100nF package="100 mil [THT, multilayer]"]
  IC24 = IC, DIP package, 20 pins [chip_label=74HC273]
  C28 = Ceramic Capacitor [capacitance=100nF package="100 mil [THT, multilayer]"]
  C18 = Ceramic Capacitor [capacitance=100nF package="100 mil [THT, multilayer]"]
  A0 = female pin header, 1 pin [form="♀ (female)"]
  A1 = female pin header, 1 pin [form="♀ (female)"]
  E1 = female pin header, 1 pin [form="♀ (female)"]
  J10 = female pin header, 1 pin [form="♀ (female)"]
  CN4 = shrouded pin header, 26 pins [form="♂ (shrouded male)"]
  12V = female pin header, 1 pin [form="♀ (female)"]
  TA1 = IC, DIP package, 18 pins [chip_label=TD62083]
  TA2 = IC, DIP package, 18 pins [chip_label=TD62083]
  TA3 = IC, DIP package, 18 pins [chip_label=TD62083]
  TA10 = IC, DIP package, 18 pins [chip_label=TD62083]
  TA11 = IC, DIP package, 18 pins [chip_label=TD62083]
  J8 = female pin header, 8 pins [form="♀ (female)"]
  E2 = female pin header, 1 pin [form="♀ (female)"]
  E3 = female pin header, 1 pin [form="♀ (female)"]
  A2 = female pin header, 1 pin [form="♀ (female)"]

nets:
  RESET: IC15.pin1, IC16.pin1, IC24.pin1, J10.pin1
  N1: IC15.pin2, TA1.pin1
  D0: IC15.pin3, IC16.pin3, IC24.pin3, J8.pin1
  D1: IC15.pin4, IC16.pin4, IC24.pin4, J8.pin2
  N2: IC15.pin5, TA1.pin2
  N3: IC15.pin6, TA1.pin3
  D2: IC15.pin7, IC16.pin7, IC24.pin7, J8.pin3
  D3: IC15.pin8, IC16.pin8, IC24.pin8, J8.pin4
  N4: IC15.pin9, TA1.pin4
  GND: IC15.pin10, IC16.pin10, GND.pin1, C20.0, C19.0, IC13.pin8, IC14.pin8, C17.0, IC24.pin10, C28.0, C18.0, TA1.pin9, TA2.pin9, TA3.pin9, TA10.pin9, TA11.pin3, TA11.pin4, TA11.pin9
  N5: IC15.pin11, IC13.pin15
  N6: IC15.pin12, TA1.pin5
  D4: IC15.pin13, IC16.pin13, IC24.pin13, J8.pin5
  D5: IC15.pin14, IC16.pin14, IC24.pin14, J8.pin6
  N7: IC15.pin15, TA1.pin6
  N8: IC15.pin16, TA1.pin7
  D6: IC15.pin17, IC16.pin17, IC24.pin17, J8.pin7
  D7: IC15.pin18, IC16.pin18, IC24.pin18, J8.pin8
  N9: IC15.pin19, TA1.pin8
  5V: IC15.pin20, IC16.pin20, 5V.pin1, C20.1, C19.1, IC13.pin16, IC14.pin16, C17.1, IC24.pin20, C28.1, C18.1
  N10: IC16.pin2, TA2.pin1
  N11: IC16.pin5, TA2.pin2
  N12: IC16.pin6, TA2.pin3
  N13: IC16.pin9, TA2.pin4
  N14: IC16.pin11, IC13.pin14
  N15: IC16.pin12, TA2.pin5
  N16: IC16.pin15, TA2.pin6
  N17: IC16.pin16, TA2.pin7
  N18: IC16.pin19, TA2.pin8
  A0: IC13.pin1, IC14.pin1, A0.pin1
  A1: IC13.pin2, IC14.pin2, A1.pin1
  ?: IC13.pin3, IC13.pin5, IC13.pin6, IC14.pin3, IC14.pin5, IC14.pin6, CN4.pin21, CN4.pin22, TA10.pin11, TA10.pin12, TA11.pin1, TA11.pin2, TA11.pin5, TA11.pin6, TA11.pin7, TA11.pin8, TA11.pin11, TA11.pin12, TA11.pin17, TA11.pin18
  E1: IC13.pin4, IC14.pin4, E1.pin1
  IC22: IC13.pin7
  IC21: IC13.pin9
  IC20: IC13.pin10
  IC19: IC13.pin11
  IC18: IC13.pin12
  IC17: IC13.pin13
  NC?: IC14.pin7, IC14.pin9, IC14.pin10, IC14.pin11, IC14.pin12, IC14.pin13
  N19: IC14.pin14, IC24.pin11
  IC23: IC14.pin15
  N20: IC24.pin2, TA10.pin1
  N21: IC24.pin5, TA10.pin2
  N22: IC24.pin6, TA10.pin3
  N23: IC24.pin9, TA10.pin4
  N24: IC24.pin12, TA10.pin5
  N25: IC24.pin15, TA10.pin6
  N26: IC24.pin16, TA10.pin7
  N27: IC24.pin19, TA10.pin8
  12V: CN4.pin1, CN4.pin2, CN4.pin3, CN4.pin4, 12V.pin1, TA1.pin10, TA2.pin10, TA3.pin10, TA10.pin10, TA11.pin10
  N28: CN4.pin5, TA1.pin18
  N29: CN4.pin6, TA1.pin17
  N30: CN4.pin7, TA1.pin16
  N31: CN4.pin8, TA1.pin15
  N32: CN4.pin9, TA1.pin14
  N33: CN4.pin10, TA1.pin13
  N34: CN4.pin11, TA1.pin12
  N35: CN4.pin12, TA1.pin11
  N36: CN4.pin13, TA2.pin18
  N37: CN4.pin14, TA2.pin17
  N38: CN4.pin15, TA2.pin16
  N39: CN4.pin16, TA2.pin15
  N40: CN4.pin17, TA2.pin14
  N41: CN4.pin18, TA2.pin13
  N42: CN4.pin19, TA2.pin12
  N43: CN4.pin20, TA2.pin11
  N44: CN4.pin23, TA3.pin18
  N45: CN4.pin24, TA3.pin17
  N46: CN4.pin25, TA11.pin14
  N47: CN4.pin26, TA11.pin13
  IC17-2: TA3.pin1
  IC17-5: TA3.pin2
  IC17-6: TA3.pin3
  IC17-9: TA3.pin4
  IC17-12: TA3.pin5
  IC17-15: TA3.pin6
  IC17-16: TA3.pin7
  IC17-19: TA3.pin8
  CN5: TA3.pin11, TA3.pin12, TA3.pin13, TA3.pin14, TA3.pin15, TA3.pin16
  CN7: TA10.pin13, TA10.pin14, TA10.pin15, TA10.pin16, TA10.pin17, TA10.pin18
  NC: TA11.pin15, TA11.pin16
  E2: E2.pin1
  E3: E3.pin1
  A2: A2.pin1

notes:
  →IC16
  →IC15
  →IC24
  D0-D3
  D4-D7
  …………
