# Fritzing sketch block_power-filter (saved by Fritzing 0.9.4)

parts:
  NF1 = IC, DIP package, 4 pins [chip_label=BNX002-01]
  C32 = Ceramic Capacitor [capacitance=2.2nF voltage=0.2kV package="100 mil [THT, multilayer]"]
  C31 = Ceramic Capacitor [capacitance=2.2nF voltage=0.2kV package="100 mil [THT, multilayer]"]
  C2 = Ceramic Capacitor [capacitance=0.1µF package="100 mil [THT, multilayer]"]
  GND = male pin header, 1 pin [form="♂ (male)"]
  +5V = male pin header, 1 pin [form="♂ (male)"]
  C3 = Ceramic Capacitor [capacitance=0.1µF package="100 mil [THT, multilayer]"]
  C1 = Electrolytic Capacitor [capacitance=100µF voltage=16V package="100 mil [THT, electrolytic]"]
  +12V = male pin header, 1 pin [form="♂ (male)"]
  CN1 = male pin header, 5 pins [form="♂ (male)"]

nets:
  5V: NF1.pin1, C2.1, CN1.pin5
  12GND/5GND: NF1.pin2, C32.0, C31.1, C2.0, CN1.pin2, CN1.pin4
  GND: NF1.pin3, GND.pin1, C3.0, C1.-
  +5V: NF1.pin4, +5V.pin1, C3.1, C1.+
  GG: C32.1, C31.0, CN1.pin1
  +12V/12V: +12V.pin1, CN1.pin3

notes:
  2200pF
  2kV
